// Logisim project Aufgabe_K-2.circ as structural Verilog: 1 circuit, main circuit main
module main (
  input  x,
  input  y,
  input  z,
  input  v
);

  wire and_1_out, and_2_out, and_3_out, nand_1_out, nand_2_out, nand_3_out, or_1_out, or_2_out, or_3_out;

  nand nand_1 (nand_1_out, x, x, y);
  or or_1 (or_1_out, x, y);
  nand nand_2 (nand_2_out, z, z, v);
  or or_2 (or_2_out, z, v);
  and and_1 (and_1_out, nand_1_out, or_1_out);
  and and_2 (and_2_out, nand_2_out, or_2_out);
  nand nand_3 (nand_3_out, and_1_out, and_1_out, and_2_out);
  or or_3 (or_3_out, and_1_out, and_2_out);
  and and_3 (and_3_out, nand_3_out, or_3_out);
  // Probe on and_3_out
endmodule
